# Fritzing sketch pcpeer-ch347f-nanoch32v203 (saved by Fritzing 1.0.3b)

parts:
  U3 = CH347F (USB to SPI/I2C/JTAG/UART, QFN28) [package=QFN28]
  U4 = nanoCH32V203 (CH32V203C8T6 dev board) [package=LQFP48]

nets:
  N1: U3.TXD1, U4.PA3/ADC3
  N2: U3.RXD1, U4.PA2/ADC2
  N3: U3.TXD0, U4.PA10
  GND: U3.GND, U4.GND
  N4: U3.RXD0, U4.PA9
